# Fritzing sketch storegg (saved by Fritzing 0.9.3b)
perfboards: 4

parts:
  Raspberry_Pi_2 = Raspberry Pi 3 [part_number=RPI-3-V1.2]  # not connected
  S17 = Reed switch [package=THT]
  S18 = Reed switch [package=THT]
  LED21 = smd LED [color="Yellow (585nm)" package="0603 [SMD]"]
  LED22 = smd LED [color="Yellow (585nm)" package="0603 [SMD]"]
  S19 = Reed switch [package=THT]
  S20 = Reed switch [package=THT]
  LED23 = smd LED [color="Yellow (585nm)" package="0603 [SMD]"]
  LED24 = smd LED [color="Yellow (585nm)" package="0603 [SMD]"]
  S22 = Reed switch [package=THT]
  LED25 = smd LED [color="Yellow (585nm)" package="0603 [SMD]"]
  LED26 = smd LED [color="Yellow (585nm)" package="0603 [SMD]"]
  S21 = Reed switch [package=THT]
  R2 = Resistor [tolerance=±5% resistance=220 package=THT]
  R3 = Resistor [tolerance=±5% resistance=220 package=THT]
  R4 = Resistor [tolerance=±5% resistance=220 package=THT]
  R5 = Resistor [tolerance=±5% resistance=220 package=THT]
  R6 = Resistor [tolerance=±5% resistance=220 package=THT]
  R12 = Resistor [tolerance=±5% resistance=220 package=THT]
  LED27 = smd LED [color="Red (633nm)" package="0603 [SMD]"]  # not connected
  LED28 = smd LED [color="Red (633nm)" package="0603 [SMD]"]  # not connected
  LED29 = smd LED [color="Red (633nm)" package="0603 [SMD]"]  # not connected
  LED30 = smd LED [color="Green (565nm)" package="0603 [SMD]"]  # not connected
  LED31 = smd LED [color="Green (565nm)" package="0603 [SMD]"]  # not connected
  LED32 = smd LED [color="Yellow (585nm)" package="0603 [SMD]"]  # not connected
  LED33 = smd LED [color="Yellow (585nm)" package="0603 [SMD]"]  # not connected
  LED34 = smd LED [color="Yellow (585nm)" package="0603 [SMD]"]  # not connected
  J2 = double row male pin header, 20 pins [form="♂ (male)"]
  J3 = double row male pin header, 20 pins [form="♂ (male)"]  # not connected
  R13 = Resistor [tolerance=±5% resistance=220 package=THT]  # not connected
  LED35 = smd LED [color="Yellow (585nm)" package="0603 [SMD]"]
  LED36 = smd LED [color="Yellow (585nm)" package="0603 [SMD]"]
  S23 = Toggle Switch [package=THT]
  S24 = Toggle Switch [package=THT]
  R14 = Resistor [tolerance=±5% resistance=220 package=THT]  # not connected
  R15 = Resistor [tolerance=±5% resistance=220 package=THT]  # not connected
  R16 = Resistor [tolerance=±5% resistance=220 package=THT]
  R17 = Resistor [tolerance=±5% resistance=220 package=THT]  # not connected
  R18 = Resistor [tolerance=±5% resistance=220 package=THT]  # not connected
  R19 = Resistor [tolerance=±5% resistance=220 package=THT]
  R20 = Resistor [tolerance=±5% resistance=220 package=THT]  # not connected
  R21 = Resistor [tolerance=±5% resistance=220 package=THT]  # not connected
  R22 = Resistor [tolerance=±5% resistance=220 package=THT]
  J6 = longpad pin header, 8 pins [form="long pad"]
  J5 = longpad pin header, 8 pins [form="long pad"]

nets:
  N1: S17.pin_1, S19.pin_1, S21.pin_1, J2.pin20, J6.pin1, J5.pin1
  N2: S17.pin_2, LED21.anode, J6.pin5, J5.pin5
  N3: S18.pin_1, LED22.anode
  N4: S18.pin_2, S20.pin_2, S22.pin_2
  N5: LED21.cathode, R12.Pin_0
  N6: LED22.cathode, R6.Pin_0
  N7: S19.pin_2, LED23.anode
  N8: S20.pin_1, LED24.anode
  N9: LED23.cathode, R2.Pin_0
  N10: LED24.cathode, R5.Pin_0
  N11: S22.pin_1, LED26.anode, J6.pin4, J5.pin4
  N12: LED25.cathode, R3.Pin_0
  N13: LED25.anode, S21.pin_2
  N14: LED26.cathode, R4.Pin_0
  N15: R3.Pin_1, R12.Pin_1
  N16: R4.Pin_1, J6.pin8, J5.pin8
  N17: J2.pin1, R22.Pin_1
  N18: LED35.cathode, S23.L1
  N19: LED35.anode, R16.Pin_0
  N20: LED36.cathode, S24.L2
  N21: LED36.anode, R19.Pin_0
  N22: J6.pin2, J5.pin2
  N23: J6.pin3, J5.pin3
  N24: J6.pin6, J5.pin6
  N25: J6.pin7, J5.pin7
